# Fritzing sketch Project (saved by Fritzing 0.9.3b)

parts:
  Part1 = Arduino Mega ADK (Rev3)
  Part2 = Bluetooth HC-05 Macho

nets:
  GND: Part1.GND, Part2.GND
  5V: Part1.5V, Part2.VCC
  N1: Part1.D0/RX0, Part2.TXD
  N2: Part1.D1/TX0, Part2.RXD

notes:
  Hall sensor signal
  and GND
